// Logisim project alu.circ as structural Verilog: 1 circuit, main circuit alu
module alu (
  input  [31:0] A,
  input  [31:0] B,
  input  [3:0] ALUSel,
  output [31:0] Result
);

  wire comparator_2_eq, comparator_3_eq, or_2_out, xor_2_out;
  wire [0:0] slt7;
  wire [31:0] add0, adder_2_out, adder_3_out, and1, divu8, mul10, mulh14, mulhu11, multiplexer_2_out,
       multiplexer_3_out, multiplexer_4_out, multiplier_3_cout, not_1_out, not_2_out, not_3_out, or2, remu9,
       sll6, sra5, srl4, sub12, xor3;

  Adder #(.width(32)) adder_1 (.a(A), .b(B), .out(add0));  // open: cin, cout
  assign and1 = A & B;  // AND_Gate and_1, 32 bits wide
  assign or2 = A | B;  // OR_Gate or_1, 32 bits wide
  assign xor3 = A ^ B;  // XOR_Gate xor_1, 32 bits wide
  Shifter #(.width(32), .shift("lr")) shifter_1 (.in(A), .\dist (B[4:0]), .out(srl4));
  Multiplexer #(.select(4), .width(32), .enable("false")) multiplexer_1 (
    .in0(add0), .in1(and1), .in2(or2), .in3(xor3), .in4(srl4), .in5(sra5), .in6(sll6),
    .in7({{31{1'b0}}, slt7[0]}), .in8(divu8), .in9(remu9), .in10(mul10), .in11(mulhu11), .in12(sub12),
    .in13(B), .in14(mulh14), .out(Result), .sel(ALUSel));  // open: in15
  Shifter #(.width(32), .shift("ar")) shifter_2 (.in(A), .\dist (B[4:0]), .out(sra5));
  Shifter #(.width(32)) shifter_3 (.in(A), .\dist (B[4:0]), .out(sll6));
  Comparator #(.width(32)) comparator_1 (.a(A), .b(B), .lt(slt7[0]));  // open: gt, eq
  Divider #(.width(32)) divider_1 (.a(A), .b(B), .out(divu8));  // open: upper, rem
  Divider #(.width(32)) divider_2 (.a(A), .b(B), .rem(remu9));  // open: out, upper
  Multiplier #(.width(32)) multiplier_1 (.a(A), .b(B), .out(mul10));  // open: cin, cout
  Multiplier #(.width(32)) multiplier_2 (.a(A), .b(B), .cout(mulhu11));  // open: out, cin
  Subtractor #(.width(32)) subtractor_1 (.a(A), .b(B), .out(sub12));  // open: bin, bout
  assign not_1_out = ~A;  // NOT_Gate not_1, 32 bits wide
  assign not_2_out = ~B;  // NOT_Gate not_2, 32 bits wide
  Adder #(.width(32)) adder_2 (.a(not_1_out), .b(32'h1), .out(adder_2_out));  // open: cin, cout
  Adder #(.width(32)) adder_3 (.a(not_2_out), .b(32'h1), .out(adder_3_out));  // open: cin, cout
  Multiplexer #(.width(32), .enable("false")) multiplexer_2 (
    .in0(A), .in1(adder_2_out), .out(multiplexer_2_out), .sel(A[31]));
  Multiplexer #(.width(32), .enable("false")) multiplexer_3 (
    .in0(B), .in1(adder_3_out), .out(multiplexer_3_out), .sel(B[31]));
  Multiplier #(.width(32)) multiplier_3 (
    .a(multiplexer_2_out), .b(multiplexer_3_out), .cout(multiplier_3_cout));  // open: out, cin
  xor xor_2 (xor_2_out, A[31], B[31]);
  Comparator #(.width(32)) comparator_2 (.a(A), .b({32{1'b0}}), .eq(comparator_2_eq));  // open: gt, lt
  Comparator #(.width(32)) comparator_3 (.a(B), .b({32{1'b0}}), .eq(comparator_3_eq));  // open: gt, lt
  Multiplexer #(.width(32), .enable("false")) multiplexer_4 (
    .in0(multiplier_3_cout), .in1(not_3_out), .out(multiplexer_4_out), .sel(xor_2_out));
  assign not_3_out = ~multiplier_3_cout;  // NOT_Gate not_3, 32 bits wide
  or or_2 (or_2_out, comparator_2_eq, comparator_3_eq);
  Multiplexer #(.width(32), .enable("false")) multiplexer_5 (
    .in0(multiplexer_4_out), .in1({32{1'b0}}), .out(mulh14), .sel(or_2_out));

  // Other names for the same wires on the sheet: bsel13[31:0] = B

  // Notes on the sheet:
  //   INPUTS to your circuit
  //   DON'T CHANGE THE LOCATIONS OF THE INPUTS AND OUTPUTS!
  //   OUTPUT from your circuit
endmodule
