// Logisim project branch_comp.circ as structural Verilog: 1 circuit, main circuit branch_comp
module branch_comp (
  input  [31:0] rs1,
  input  [31:0] rs2,
  input  BrUn,
  output BrEq,
  output BrLt
);

  wire EqSigned, EqUnsigned, LTSigned, LTUnsigned;

  Comparator #(.width(32)) comparator_1 (.a(rs1), .b(rs2), .eq(EqSigned));  // open: gt, lt
  Comparator #(.width(32), .mode("unsigned")) comparator_2 (.a(rs1), .b(rs2), .eq(EqUnsigned));  // open: gt, lt
  Comparator #(.width(32)) comparator_3 (.a(rs1), .b(rs2), .lt(LTSigned));  // open: gt, eq
  Comparator #(.width(32), .mode("unsigned")) comparator_4 (.a(rs1), .b(rs2), .lt(LTUnsigned));  // open: gt, eq
  Multiplexer #(.enable("false")) multiplexer_1 (.in0(EqSigned), .in1(EqUnsigned), .out(BrEq), .sel(BrUn));
  Multiplexer #(.enable("false")) multiplexer_2 (.in0(LTSigned), .in1(LTUnsigned), .out(BrLt), .sel(BrUn));

  // Notes on the sheet:
  //   INPUTS to your circuit
  //   DON'T CHANGE THE LOCATIONS OF THE INPUTS AND OUTPUTS!
  //   OUTPUT from your circuit
endmodule
