// Logisim project control_logic.circ as structural Verilog: 1 circuit, main circuit control_logic
module control_logic (
  input  [31:0] inst,
  input  BrEq,
  input  BrLt,
  output PCSel,
  output RegWEn,
  output [2:0] ImmSel,
  output BrUn,
  output ASel,
  output BSel,
  output [3:0] ALUSel,
  output MemRW,
  output [1:0] WBSel
);

  wire add, addi, and1, and_29_out, and_30_out, and_31_out, andi, beq, blt, bne, divu, Funct3_0x0,
       Funct3_0x1, Funct3_0x2, Funct3_0x3, Funct3_0x4, Funct3_0x5, Funct3_0x6, Funct3_0x7, Funct7_0x00,
       Funct7_0x01, Funct7_0x20, jal, jalr, lb, lh, lui, lw, mul, mulh, mulhu, not_1_out, Op_0x03, Op_0x13,
       Op_0x33, Op_0x63, Op_0x67, or1, or_1_out, or_6_out, or_7_out, or_8_out, or_9_out, or_10_out,
       or_11_out, or_12_out, or_13_out, or_14_out, or_15_out, or_16_out, ori, priority_encoder_2_en_out,
       remu, sll1, slli, slt, slti, sra1, srai, srl1, srli, sub, sw, xor1, xori;
  wire [1:0] multiplexer_1_out;
  wire [3:0] priority_encoder_2_out;

  Comparator #(.width(7)) comparator_1 (.a(inst[6:0]), .b(7'b0110011), .eq(Op_0x33));  // open: gt, lt
  Comparator #(.width(7)) comparator_2 (.a(inst[6:0]), .b(7'b0000011), .eq(Op_0x03));  // open: gt, lt
  Comparator #(.width(7)) comparator_3 (.a(inst[6:0]), .b(7'b0010011), .eq(Op_0x13));  // open: gt, lt
  Comparator #(.width(7)) comparator_4 (.a(inst[6:0]), .b(7'b1100111), .eq(Op_0x67));  // open: gt, lt
  Comparator #(.width(7)) comparator_5 (.a(inst[6:0]), .b(7'b0100011), .eq(MemRW));  // open: gt, lt
  Comparator #(.width(7)) comparator_6 (.a(inst[6:0]), .b(7'b1100011), .eq(Op_0x63));  // open: gt, lt
  Comparator #(.width(7)) comparator_7 (.a(inst[6:0]), .b(7'b0110111), .eq(lui));  // open: gt, lt
  Comparator #(.width(7)) comparator_8 (.a(inst[6:0]), .b(7'b1101111), .eq(jal));  // open: gt, lt
  and and_1 (add, Op_0x33, Funct3_0x0, Funct7_0x00);
  and and_2 (mul, Op_0x33, Funct3_0x0, Funct7_0x01);
  and and_3 (sub, Op_0x33, Funct3_0x0, Funct7_0x20);
  and and_4 (lb, Op_0x03, Funct3_0x0);
  and and_5 (lh, Op_0x03, Funct3_0x1);
  and and_6 (lw, Op_0x03, Funct3_0x2);
  and and_7 (beq, Op_0x63, Funct3_0x0);
  and and_8 (blt, Op_0x63, Funct3_0x4);
  and and_9 (BrUn, Op_0x63, Funct3_0x6);
  and and_10 (sll1, Op_0x33, Funct3_0x1, Funct7_0x00);
  and and_11 (mulh, Op_0x33, Funct3_0x1, Funct7_0x01);
  and and_12 (addi, Op_0x13, Funct3_0x0);
  and and_13 (slli, Op_0x13, Funct3_0x1, Funct7_0x00);
  and and_14 (slti, Op_0x13, Funct3_0x2);
  and and_15 (bne, Op_0x63, Funct3_0x1);
  and and_16 (jalr, Op_0x67, Funct3_0x0);
  Comparator #(.width(3)) comparator_9 (.a(inst[14:12]), .b(3'b000), .eq(Funct3_0x0));  // open: gt, lt
  Comparator #(.width(3)) comparator_10 (.a(inst[14:12]), .b(3'b001), .eq(Funct3_0x1));  // open: gt, lt
  Comparator #(.width(3)) comparator_11 (.a(inst[14:12]), .b(3'b010), .eq(Funct3_0x2));  // open: gt, lt
  Comparator #(.width(3)) comparator_12 (.a(inst[14:12]), .b(3'b011), .eq(Funct3_0x3));  // open: gt, lt
  Comparator #(.width(3)) comparator_13 (.a(inst[14:12]), .b(3'b100), .eq(Funct3_0x4));  // open: gt, lt
  Comparator #(.width(3)) comparator_14 (.a(inst[14:12]), .b(3'b101), .eq(Funct3_0x5));  // open: gt, lt
  Comparator #(.width(3)) comparator_15 (.a(inst[14:12]), .b(3'b110), .eq(Funct3_0x6));  // open: gt, lt
  Comparator #(.width(3)) comparator_16 (.a(inst[14:12]), .b(3'b111), .eq(Funct3_0x7));  // open: gt, lt
  and and_17 (mulhu, Op_0x33, Funct3_0x3, Funct7_0x01);
  and and_18 (slt, Op_0x33, Funct3_0x2, Funct7_0x00);
  and and_19 (xor1, Op_0x33, Funct3_0x4, Funct7_0x00);
  and and_20 (xori, Op_0x13, Funct3_0x4);
  and and_21 (srli, Op_0x13, Funct3_0x5, Funct7_0x00);
  and and_22 (srai, Op_0x13, Funct3_0x5, Funct7_0x20);
  Comparator #(.width(7)) comparator_17 (.a(inst[31:25]), .b({7{1'b0}}), .eq(Funct7_0x00));  // open: gt, lt
  Comparator #(.width(7)) comparator_18 (.a(inst[31:25]), .b(7'b0000001), .eq(Funct7_0x01));  // open: gt, lt
  Comparator #(.width(7)) comparator_19 (.a(inst[31:25]), .b(7'b0100000), .eq(Funct7_0x20));  // open: gt, lt
  and and_23 (divu, Op_0x33, Funct3_0x5, Funct7_0x01);
  and and_24 (srl1, Op_0x33, Funct3_0x5, Funct7_0x00);
  and and_25 (sra1, Op_0x33, Funct3_0x5, Funct7_0x20);
  and and_26 (ori, Op_0x13, Funct3_0x6);
  and and_27 (andi, Op_0x13, Funct3_0x7);
  and and_28 (sw, MemRW, Funct3_0x2);
  not not_1 (not_1_out, BrEq);
  and and_29 (and_29_out, not_1_out, bne);
  or or_1 (or_1_out, blt, BrUn);
  or or_2 (RegWEn, Op_0x33, Op_0x03, Op_0x13, lui, jal, Op_0x67);
  or or_3 (BSel, Op_0x03, Op_0x63, Op_0x13, Op_0x67, lui, jal, MemRW);
  and and_30 (and_30_out, BrEq, beq);
  and and_31 (and_31_out, BrLt, or_1_out);
  and and_32 (or1, Op_0x33, Funct3_0x6, Funct7_0x00);
  and and_33 (remu, Op_0x33, Funct3_0x7, Funct7_0x01);
  and and_34 (and1, Op_0x33, Funct3_0x7, Funct7_0x00);
  or or_4 (PCSel, and_30_out, and_29_out, jal, Op_0x67, and_31_out);
  or or_5 (ASel, jal, Op_0x63);
  or or_6 (or_6_out, add, addi);
  or or_7 (or_7_out, and1, andi);
  or or_8 (or_8_out, or1, ori);
  or or_9 (or_9_out, xor1, xori);
  or or_10 (or_10_out, srl1, srli);
  or or_11 (or_11_out, sra1, srai);
  or or_12 (or_12_out, sll1, slli);
  or or_13 (or_13_out, slt, slti);
  Multiplexer #(.width(2), .enable("false")) multiplexer_1 (
    .in0(2'b01), .in1(2'b00), .out(multiplexer_1_out), .sel(or_14_out));
  or or_14 (or_14_out, Op_0x03, MemRW);
  or or_15 (or_15_out, Op_0x67, jal);
  or or_16 (or_16_out, Op_0x03, Op_0x13, Op_0x67);
  Multiplexer #(.width(2), .enable("false")) multiplexer_2 (
    .in0(multiplexer_1_out), .in1(2'b10), .out(WBSel), .sel(or_15_out));
  Priority_Encoder priority_encoder_1 (
    .in0(or_16_out), .in1(MemRW), .in2(Op_0x63), .in3(lui), .in4(jal), .out(ImmSel));  // open: in5, in6, in7, en_in, gs, en_out
  Priority_Encoder #(.select(4)) priority_encoder_2 (
    .in0(or_6_out), .in1(or_7_out), .in2(or_8_out), .in3(or_9_out), .in4(or_10_out), .in5(or_11_out),
    .in6(or_12_out), .in7(or_13_out), .in8(divu), .in9(remu), .in10(mul), .in11(mulhu), .in12(sub),
    .in13(lui), .in14(mulh), .out(priority_encoder_2_out), .en_out(priority_encoder_2_en_out));  // open: in15, gs, en_in
  Multiplexer #(.width(4), .enable("false")) multiplexer_3 (
    .in0(priority_encoder_2_out), .in1(4'b0000), .out(ALUSel), .sel(priority_encoder_2_en_out));

  // Other names for the same wires on the sheet: bltu = BrUn; Opcode[6:0] = inst[6:0]; Funct3[2:0] = inst[14:12];
  //   Funct7[6:0] = inst[31:25]; Op_0x6f = jal; Op_0x37 = lui; Op_0x23 = MemRW

  // Notes on the sheet:
  //   INPUTS to your circuit
  //   DON'T CHANGE THE LOCATIONS OF THE INPUTS AND OUTPUTS!
  //   OUTPUT from your circuit
  //   Immsel Values: 0: I, 1: S, 2: B, 3: U, 4: J
endmodule
