// Logisim project imm_gen.circ as structural Verilog: 1 circuit, main circuit imm_gen
module imm_gen (
  input  [31:0] inst,
  input  [2:0] ImmSel,
  output [31:0] imm
);

  wire [31:0] B_2, I_0, J_4, S_1, U_3;

  assign I_0 = {{20{inst[31]}}, inst[31:20]};  // Bit_Extender bit_extender_1
  assign S_1 = {{20{inst[31]}}, {inst[31:25], inst[11:7]}};  // Bit_Extender bit_extender_2
  assign B_2 = {{19{inst[31]}}, {inst[31], inst[7], inst[30:25], inst[11:8], 1'b0}};  // Bit_Extender bit_extender_3
  Bit_Extender #(.in_width(32), .out_width(32)) bit_extender_4 (.in({inst[31:12], {12{1'b0}}}), .out(U_3));
  assign J_4 = {{11{inst[31]}}, {inst[31], inst[19:12], inst[20], inst[30:21], 1'b0}};  // Bit_Extender bit_extender_5
  Multiplexer #(.select(3), .width(32), .enable("false")) multiplexer_1 (
    .in0(I_0), .in1(S_1), .in2(B_2), .in3(U_3), .in4(J_4), .out(imm), .sel(ImmSel));  // open: in5, in6, in7

  // Notes on the sheet:
  //   INPUTS to your circuit
  //   Immsel Values: 0: I, 1: S, 2: B, 3: U, 4: J
  //   DON'T CHANGE THE LOCATIONS OF THE INPUTS AND OUTPUTS!
  //   OUTPUT from your circuit
endmodule
